# Fritzing sketch clock (saved by Fritzing 0.9.2b)
circuit board: 1.77129cm x 3.99973cm
breadboards: 1

parts:
  R1 = Resistor [tolerance=±5% resistance=220 package=THT]
  S1 = Pushbutton [package="[THT]"]
  R2 = PHOTOCELL [package=photocell]
  R3 = Resistor [tolerance=±5% resistance=220 package=THT]

nets:
  N1: R1.Pin_0, S1.Pin_1, S1.Pin_2
  N2: R1.Pin_1, R3.Pin_0
  N3: S1.Pin_3, S1.Pin_4, R2.P$1
  N4: R2.P$2, R3.Pin_1

notes:
  D
  VCC
  GND
  A
